# Fritzing sketch traffic_light_schema (saved by Fritzing 0.7.11b)
breadboards: 1

parts:
  U1 = Arduino Mega
  Arduino_Ethernet_Shield1 = Arduino Ethernet Shield  # not connected
  R6 = Resistor [tolerance=±5% resistance=1.5 package=THT]
  Q1 = NPN-Transistor [part_number=C547B package="TO92 [THT]"]
  Power_plug1 = Power plug
  R7 = Resistor [tolerance=±5% resistance=1.5 package=THT]
  Q2 = NPN-Transistor [part_number=C547B package="TO92 [THT]"]
  R8 = Resistor [tolerance=±5% resistance=1.5 package=THT]
  Q3 = NPN-Transistor [part_number=C547B package="TO92 [THT]"]
  R9 = Resistor [tolerance=±5% resistance=1.5 package=THT]
  Q4 = NPN-Transistor [part_number=C547B package="TO92 [THT]"]
  R10 = Resistor [tolerance=±5% resistance=1.5 package=THT]
  Q5 = NPN-Transistor [part_number=C547B package="TO92 [THT]"]
  R11 = Resistor [tolerance=±5% resistance=1.5 package=THT]
  Q6 = NPN-Transistor [part_number=C547B package="TO92 [THT]"]
  R12 = Resistor [tolerance=±5% resistance=1.5 package=THT]
  Q7 = NPN-Transistor [part_number=C547B package="TO92 [THT]"]
  R13 = Resistor [tolerance=±5% resistance=1.5 package=THT]
  Q8 = NPN-Transistor [part_number=C547B package="TO92 [THT]"]
  R14 = Resistor [tolerance=±5% resistance=1.5 package=THT]
  Q9 = NPN-Transistor [part_number=C547B package="TO92 [THT]"]
  R15 = Resistor [tolerance=±5% resistance=1.5 package=THT]
  Q10 = NPN-Transistor [part_number=C547B package="TO92 [THT]"]
  LED1 = LED - 5mm [color="White (6500K)" package="5 mm [THT]"]
  R16 = Resistor [tolerance=±5% resistance=120 package=THT]
  LED2 = LED - 5mm [color="White (6500K)" package="5 mm [THT]"]
  R17 = Resistor [tolerance=±5% resistance=120 package=THT]
  LED3 = LED - 5mm [color="White (6500K)" package="5 mm [THT]"]
  R18 = Resistor [tolerance=±5% resistance=120 package=THT]
  LED4 = LED - 5mm [color="White (6500K)" package="5 mm [THT]"]
  R19 = Resistor [tolerance=±5% resistance=120 package=THT]
  LED5 = LED - 5mm [color="White (6500K)" package="5 mm [THT]"]
  R20 = Resistor [tolerance=±5% resistance=120 package=THT]
  LED6 = LED - 5mm [color="White (6500K)" package="5 mm [THT]"]
  R21 = Resistor [tolerance=±5% resistance=120 package=THT]
  LED7 = LED - 5mm [color="White (6500K)" package="5 mm [THT]"]
  R22 = Resistor [tolerance=±5% resistance=120 package=THT]
  LED8 = LED - 5mm [color="White (6500K)" package="5 mm [THT]"]
  R23 = Resistor [tolerance=±5% resistance=120 package=THT]
  LED9 = LED - 5mm [color="White (6500K)" package="5 mm [THT]"]
  R24 = Resistor [tolerance=±5% resistance=120 package=THT]
  LED10 = LED - 5mm [color="White (6500K)" package="5 mm [THT]"]
  R25 = Resistor [tolerance=±5% resistance=120 package=THT]

nets:
  N1: U1.D22, R15.Pin_1
  N2: U1.D23, R6.Pin_0
  N3: U1.D24, R14.Pin_0
  N4: U1.D25, R7.Pin_0
  N5: U1.D26, R13.Pin_0
  N6: U1.D27, R8.Pin_0
  N7: U1.D28, R12.Pin_0
  N8: U1.D29, R9.Pin_0
  N9: U1.D30, R11.Pin_0
  N10: U1.D31, R10.Pin_0
  N11: R6.Pin_1, Q1.B
  N12: Q1.E, LED1.cathode
  N13: Q1.C, Power_plug1.GND, Q2.C, Q3.C, Q4.C, Q5.C, Q6.C, Q7.C, Q8.C, Q9.C, Q10.C
  N14: Power_plug1.VCC, R16.Pin_1, R17.Pin_1, R18.Pin_1, R19.Pin_1, R20.Pin_1, R21.Pin_1, R22.Pin_1, R23.Pin_1, R24.Pin_1, R25.Pin_1
  N15: R7.Pin_1, Q2.B
  N16: Q2.E, LED2.cathode
  N17: R8.Pin_1, Q3.B
  N18: Q3.E, LED3.cathode
  N19: R9.Pin_1, Q4.B
  N20: Q4.E, LED4.cathode
  N21: R10.Pin_1, Q5.B
  N22: Q5.E, LED5.cathode
  N23: R11.Pin_1, Q6.B
  N24: Q6.E, LED6.cathode
  N25: R12.Pin_1, Q7.B
  N26: Q7.E, LED7.cathode
  N27: R13.Pin_1, Q8.B
  N28: Q8.E, LED8.cathode
  N29: R14.Pin_1, Q9.B
  N30: Q9.E, LED9.cathode
  N31: R15.Pin_0, Q10.B
  N32: Q10.E, LED10.cathode

notes:
  5V Netzteil
  LED SUPERHELL WHITE (2,8V bis 3,8V; 20 mA)
  Netzwerkanschluss
  Arduino 5V
  C547B Transistor
  1,5 kOhm Widerstand
  120 Ohm Widerstand
  LED
